# Fritzing sketch iot apis (saved by Fritzing 0.9.3b)
breadboards: 1

parts:
  hc-sr1 = hc-sr04
  Moisture_Sensor = Soil Moisture Sensor
  Leak_Sensor = Soil Moisture Sensor
  M1 = DC Motor
  Q1 = TRANSISTOR_NPN [package=to-92]
  R1 = Resistor [tolerance=±5% resistance=1k package="2512 [SMD]"]
  D1 = Diode [package=diode-1n4148]
  C1 = Ceramic Capacitor [capacitance=100nF package="100 mil [THT, multilayer]"]
  R3 = Resistor [tolerance=±5% resistance=10k package="2512 [SMD]"]
  BAT1 = Battery Holders [package=battery-aa-panel]
  U1 = NodeMCU V1.0
  LED1 = RGB LED (com. cathode, rgb) [package="5 mm [THT]"]
  R4 = Resistor [tolerance=±5% resistance=47 package="2512 [SMD]"]
  R5 = Resistor [tolerance=±5% resistance=100 package="2512 [SMD]"]
  R6 = Resistor [tolerance=±5% resistance=100 package="2512 [SMD]"]

nets:
  VCC: hc-sr1.VCC, U1.3V3
  N1: hc-sr1.Echo, U1.D3
  GND: hc-sr1.GND, Moisture_Sensor.GND, Q1.E, BAT1.-, LED1.common_cathode
  N2: Moisture_Sensor.VCC, R3.Pin_0, U1.A0
  GND_2: Leak_Sensor.GND, U1.GND
  N3: Leak_Sensor.VCC, U1.D5
  N4: M1.pin_1, Q1.C, C1.1
  N5: M1.pin_2, D1.C, C1.0, BAT1.+
  N6: Q1.B, R1.Pin_1
  N7: R1.Pin_0, U1.D2
  N8: R3.Pin_1, U1.D8
  N9: U1.D0, U1.RST
  N10: U1.D1, R5.Pin_1
  N11: U1.D6, R6.Pin_1
  N12: U1.SD3, R4.Pin_1
  N13: LED1.red_anode, R4.Pin_0
  N14: LED1.green_anode, R5.Pin_0
  N15: LED1.blue_anode, R6.Pin_0

notes:
  Pump
  USB power source
  5v
  Soil probe
  Leak probe
  Resistors, left to right:
  R1 - 10 KOhm
  R2 - 1 KOhm
  R3 - 470 Ohm
  R4 - 1 KOhm
  R5 - 47 Ohm
  R6 - 100 Ohm
  R7 - 100 Ohm
  Transistor: PN2222A
  Capacitor: 0.1uF
  Diode: 1N4001
  LED: Common Cathode RGB
  Water level sensor
  (based on 3pin
  Grove ultrasonic sensor)

custom parts:
  NodeMCU V1.0: ESP8266 based NodeMCU
